// Logisim project cpu.circ as structural Verilog: 3 circuits, main circuit CPU
module CPU (
  input  [31:0] Instruction,
  input  CLK,
  output [31:0] s0,
  output [31:0] s1,
  output [31:0] t0,
  output [31:0] t1,
  output [31:0] a0,
  output [31:0] ra,
  output [31:0] sp,
  output [31:0] PC
);

  wire [31:0] pc_4, pc_t, plus_4;

  // Incrementer incrementer_1: pin names not known; wires that end beside it: plus_4
  Register #(.width(32)) register_1 (.D(pc_4), .Q(PC), .clk(CLK));  // open: en, clr
  // PC pc_1: pin names not known; wires that end beside it: pc_t
  Adder #(.width(32)) adder_1 (.a(pc_t), .b(plus_4), .out(pc_4));  // open: cin, cout
  // RegFile regfile_1: pin names not known
  // ALU alu_1: pin names not known
  // memory_main main_1: pin names not known

  assign {Instruction[30:25], Instruction[23:20], Instruction[18:15], Instruction[13:12], Instruction[10:7], Instruction[5:0]} = {{6{Instruction[31]}}, {4{Instruction[24]}}, {4{Instruction[19]}}, {2{Instruction[14]}}, {4{Instruction[11]}}, {6{Instruction[6]}}};

  // Other names for the same wires on the sheet: fetch_addr[31:0] = PC;
  //   INST[31:0] = {{7{Instruction[31]}}, {5{Instruction[24]}}, {5{Instruction[19]}}, {3{Instruction[14]}}, {5{Instruction[11]}}, {7{Instruction[6]}}};
  //   opcode = Instruction[6]; rd = Instruction[11]; funct3 = Instruction[14]; rs1 = Instruction[19];
  //   rs2 = Instruction[24]; funct7 = Instruction[31]

  // Notes on the sheet:
  //   NOTE
  //   Please do not modify/replace/move/change/delete/etc input and output pins
  //   These are debug/test outputs from your circuit
endmodule

module ImmGen (
  input  [31:0] Instruction,
  input  [2:0] in_2,
  output [31:0] Immediate
);

  wire [31:0] tipo_B, tipo_I, tipo_S;

  assign tipo_I = {{20{Instruction[31]}}, Instruction[31:20]};  // Bit_Extender bit_extender_1
  assign tipo_S = {{20{Instruction[31]}}, {Instruction[31:25], Instruction[11:7]}};  // Bit_Extender bit_extender_2
  assign tipo_B = {{20{Instruction[7]}}, {Instruction[7], Instruction[30:25], Instruction[11:8], 1'b0}};  // Bit_Extender bit_extender_3
  Multiplexer #(.select(3), .width(32)) multiplexer_1 (
    .in0(tipo_I), .in1(tipo_S), .in2(tipo_B), .in3({Instruction[31:12], {12{1'b0}}}),
    .in4({{12{1'b0}}, Instruction[31], Instruction[19:13], Instruction[20], Instruction[30:21], 1'b0}),
    .in5({32{1'b0}}), .in6({32{1'b0}}), .in7({32{1'b0}}), .out(Immediate), .sel(in_2));  // open: en

  // Other names for the same wires on the sheet: instruc[31:0] = Instruction; Immedate[31:0] = Immediate;
  //   ImmSel[2:0] = in_2; tipo_J[19:1] = {Instruction[31], Instruction[19:13], Instruction[20], Instruction[30:21]};
  //   tipo_U[31:12] = Instruction[31:12]

  // Notes on the sheet:
  //   Inputs
  //   TIPO I
  //   TIPO S
  //   TIPO B
  //   Extras:
  //   Output:
  //   TIPO U
  //   TIPO J
endmodule

module ControlUnit (
  input  [6:0] in_1,
  input  [2:0] in_2,
  input  [6:0] in_3,
  input  in_4,
  output out_5,
  output out_6,
  output out_7,
  output out_8,
  output [2:0] out_9,
  output [3:0] out_10,
  output [1:0] out_11
);

  ROM #(.addrWidth(7), .dataWidth(13)) rom_1 (
    .addr(in_1), .data({out_5, out_6, out_7, out_8, out_9, out_10, out_11}), .sel(in_4));

  // Other names for the same wires on the sheet: ALUsrc = out_8; MemWrite = out_7; MemRead = out_6; RegWrite = out_5;
  //   ALUop[3:0] = out_10; funct3[2:0] = in_2; funct7[6:0] = in_3; ImmSel[2:0] = out_9; opcode[6:0] = in_1;
  //   PCSel[1:0] = out_11

  // Notes on the sheet:
  //   Inputs
  //   Outputs
endmodule
