// Logisim project regfile.circ as structural Verilog: 2 circuits, main circuit RegFile
module RegFile (
  input  [4:0] RD,
  input  [4:0] RS1,
  input  [4:0] RS2,
  input  [31:0] W,
  input  WE,
  input  Clk,
  output [31:0] s0,
  output [31:0] s1,
  output [31:0] t0,
  output [31:0] t1,
  output [31:0] a0,
  output [31:0] ra,
  output [31:0] sp,
  output [31:0] R1,
  output [31:0] R2
);

  Register #(.width(32)) x0_zero ();  // open: D, en, Q, clk, clr
  Register #(.width(32)) x1_ra ();  // open: D, en, Q, clk, clr
  Register #(.width(32)) x2_sp ();  // open: D, en, Q, clk, clr
  Register #(.width(32)) x5_t0 ();  // open: D, en, Q, clk, clr
  Register #(.width(32)) x6_t1 ();  // open: D, en, Q, clk, clr
  Register #(.width(32)) x8_s0 ();  // open: D, en, Q, clk, clr
  Register #(.width(32)) x9_s1 ();  // open: D, en, Q, clk, clr
  Register #(.width(32)) x10_a0 ();  // open: D, en, Q, clk, clr
  Register #(.width(32)) x11_a1 ();  // open: D, en, Q, clk, clr

  // Notes on the sheet:
  //   Write Register
  //   Read Register 1
  //   Read Register 2
  //   Write Data
  //   Write Enable
  //   Clock
  //   NOTE
  //   Please do not modify/replace/move/change/delete/etc input and output pins
  //   These are debug/test outputs from your circuit
  //   Read Data 1
  //   Read Data 2
endmodule

module Decoder (
  input  [31:0] Instruccion
);


  assign {Instruccion[30:25], Instruccion[23:20], Instruccion[18:15], Instruccion[13:12], Instruccion[10:7], Instruccion[5:0]} = {{6{Instruccion[31]}}, {4{Instruccion[24]}}, {4{Instruccion[19]}}, {2{Instruccion[14]}}, {4{Instruccion[11]}}, {6{Instruccion[6]}}};

  // Other names for the same wires on the sheet: Opcode = Instruccion[6]; rd = Instruccion[11];
  //   funct3 = Instruccion[14]; rs1 = Instruccion[19]; rs2 = Instruccion[24]; funct7 = Instruccion[31]
endmodule
